# Fritzing sketch LED_7segment_bitbang (saved by Fritzing 0.9.3b)
circuit board: 5.09207cm x 4.04515cm
breadboards: 1

parts:
  J4 = female pin header, 5 pins [form="♀ (female)"]
  J2 = female pin header, 5 pins [form="♀ (female)"]
  Q1 = NPN-Transistor [package="TO92 [THT]"]
  R1 = Resistor [tolerance=±5% resistance=470 package=THT]
  R2 = Resistor [tolerance=±5% resistance=470 package=THT]
  R3 = Resistor [tolerance=±5% resistance=470 package=THT]
  R4 = Resistor [tolerance=±5% resistance=470 package=THT]
  R5 = Resistor [tolerance=±5% resistance=470 package=THT]
  R6 = Resistor [tolerance=±5% resistance=470 package=THT]
  R7 = Resistor [tolerance=±5% resistance=470 package=THT]
  Q2 = NPN-Transistor [package="TO92 [THT]"]
  Q3 = NPN-Transistor [package="TO92 [THT]"]
  J3 = shrouded pin header, 12 pins [form="♂ (shrouded male)"]
  R8 = Resistor [tolerance=±5% resistance=1k package=THT]
  R9 = Resistor [tolerance=±5% resistance=1k package=THT]
  R10 = Resistor [tolerance=±5% resistance=1k package=THT]

nets:
  N1: J4.pin1, R1.Pin_1
  N2: J4.pin2, R2.Pin_1
  N3: J4.pin3, R3.Pin_1
  N4: J4.pin4, R4.Pin_1
  N5: J4.pin5, Q3.E
  N6: J2.pin1, Q2.E
  N7: J2.pin2, R7.Pin_0
  N8: J2.pin3, R6.Pin_0
  N9: J2.pin4, Q1.E
  N10: J2.pin5, R5.Pin_0
  N11: Q1.B, R9.Pin_1
  N12: Q1.C, Q2.C, Q3.C, J3.pin6
  N13: R1.Pin_0, J3.pin2
  N14: R2.Pin_0, J3.pin1
  N15: R3.Pin_0, J3.pin12
  N16: R4.Pin_0, J3.pin11
  N17: R5.Pin_1, J3.pin10
  N18: R6.Pin_1, J3.pin9
  N19: R7.Pin_1, J3.pin8
  N20: Q2.B, R8.Pin_1
  N21: Q3.B, R10.Pin_0
  N22: J3.pin3, R10.Pin_1
  N23: J3.pin4, R8.Pin_0
  N24: J3.pin5, R9.Pin_0
